// Logisim project mycpu.circ as structural Verilog: 9 circuits, main circuit main
module main (
  input  exp0,
  input  _1,
  input  _2
);

  wire ALUSrc, and_1_out, and_2_out, BneOrBeq, Branch, clk, clock_1_out, Equal, ExpBlock, ExRegWrite, Halt,
       HasExp, IsCOP0, IsEret, IsJAL, IsJR, IsShamt, IsSyscall, Jump, MemRead, MemtoReg, MemWrite,
       multiplexer_4_out, multiplexer_11_out, not_1_out, not_2_out, not_3_out, not_4_out, not_5_out,
       or_1_out, RegDst, RegWrite, xor_1_out, ZeroExtend;
  wire [3:0] adder_2_out, ALOop, syscalldecoder_1_out_6_2, syscalldecoder_1_out_6_3, syscalldecoder_1_out_6_4;
  wire [4:0] multiplexer_6_out, multiplexer_7_out, multiplexer_8_out, multiplexer_9_out;
  wire [8:0] demultiplexer_1_out0, demultiplexer_1_out1;
  wire [19:0] syscalldecoder_1_out_6;
  wire [27:0] adder_2_out_2;
  wire [31:0] adder_1_out, adder_3_out, alu_1_result1, bit_extender_1_out, cop0_1_dout, cop0_1_pcout,
       immeextend_1_out_3, multiplexer_1_out, multiplexer_3_out, multiplexer_5_out, multiplexer_10_out,
       multiplexer_12_out, multiplexer_13_out, multiplexer_14_out, multiplexer_15_out, multiplexer_16_out,
       multiplexer_17_out, multiplexer_18_out, multiplexer_19_out, PC_q, ram_1_data, regfile_1_r1,
       regfile_1_r2, register_1_q, rom_1_data, rom_2_data, shifter_1_out;

  and and_1 (and_1_out, IsEret, IsCOP0);
  Multiplexer #(.select(1), .width(32), .disabled("Z"), .enable("false")) multiplexer_1 (
    .in0(multiplexer_18_out), .in1(cop0_1_pcout), .out(multiplexer_1_out), .sel(and_1_out));
  Multiplexer #(.select(1), .width(1), .disabled("Z"), .enable("false")) multiplexer_2 (
    .in0(clock_1_out), .in1(1'b1), .out(clk), .sel(Halt));
  Clock #(.highDuration(1), .lowDuration(1)) clock_1 (.out(clock_1_out));
  Multiplexer #(.select(1), .width(32), .disabled("Z"), .enable("false")) multiplexer_3 (
    .in0(32'h800), .in1(multiplexer_1_out), .out(multiplexer_3_out), .sel(not_1_out));
  not not_1 (not_1_out, HasExp);
  or or_1 (or_1_out, HasExp, and_1_out);
  Multiplexer #(.select(1), .width(1), .disabled("Z"), .enable("false")) multiplexer_4 (
    .in0(clk), .in1(not_2_out), .out(multiplexer_4_out), .sel(or_1_out));
  not not_2 (not_2_out, clk);
  Register #(.width(32), .trigger("rising"), .Select("low")) PC (
    .D(multiplexer_3_out), .Q(PC_q), .clk(multiplexer_4_out));  // open: en, clr
  Demultiplexer #(.select(1), .width(9), .tristate("false"), .disabled("Z"), .enable("false")) demultiplexer_1 (
    .out0(demultiplexer_1_out0), .out1(demultiplexer_1_out1), .in(PC_q[10:2]), .sel(PC_q[11]));
  Adder #(.width(32)) adder_1 (.a(PC_q), .b(32'h4), .out(adder_1_out));  // open: cin, cout
  Adder #(.width(32)) adder_2 (.a(PC_q), .b(32'h4), .out({adder_2_out, adder_2_out_2}));  // open: cin, cout
  ROM #(.addrWidth(9), .dataWidth(32), .Select("low")) rom_1 (.addr(demultiplexer_1_out0), .data(rom_1_data));
  ROM #(.addrWidth(9), .dataWidth(32), .Select("low")) rom_2 (.addr(demultiplexer_1_out1), .data(rom_2_data));
  Multiplexer #(.select(1), .width(32), .disabled("Z"), .enable("false")) multiplexer_5 (
    .in0(rom_1_data), .in1(rom_2_data), .out(multiplexer_5_out), .sel(PC_q[11]));
  Control control_1 (
    .op(multiplexer_5_out[31:26]), .Funct(multiplexer_5_out[5:0]), .IsJAL(IsJAL), .IsShamt(IsShamt),
    .MemtoReg(MemtoReg), .RegWrite(RegWrite), .BneOrBeq(BneOrBeq), .ALUSrc(ALUSrc), .IsSyscal(IsSyscall),
    .ZeroExtend(ZeroExtend), .MemRead(MemRead), .MemWrite(MemWrite), .Jump(Jump), .Branch(Branch),
    .RegDst(RegDst), .IsJR(IsJR), .IsCOP0(IsCOP0), .out_18(ALOop));
  Multiplexer #(.select(1), .width(5), .disabled("Z"), .enable("false")) multiplexer_6 (
    .in0(multiplexer_5_out[20:16]), .in1(multiplexer_5_out[15:11]), .out(multiplexer_6_out), .sel(RegDst));
  Multiplexer #(.select(1), .width(5), .disabled("Z"), .enable("false")) multiplexer_7 (
    .in0(multiplexer_5_out[25:21]), .in1(5'b00010), .out(multiplexer_7_out), .sel(IsSyscall));
  Multiplexer #(.select(1), .width(5), .disabled("Z"), .enable("false")) multiplexer_8 (
    .in0(multiplexer_5_out[20:16]), .in1(5'b00100), .out(multiplexer_8_out), .sel(IsSyscall));
  Multiplexer #(.select(1), .width(5), .disabled("Z"), .enable("false")) multiplexer_9 (
    .in0(multiplexer_6_out), .in1({5{1'b1}}), .out(multiplexer_9_out), .sel(IsJAL));
  not not_3 (not_3_out, IsCOP0);
  Register #(.width(32), .trigger("rising"), .Select("low")) register_1 (
    .D(PC_q), .Q(register_1_q), .clk(HasExp));  // open: en, clr
  Multiplexer #(.select(1), .width(32), .disabled("Z"), .enable("false")) multiplexer_10 (
    .in0(cop0_1_dout), .in1(multiplexer_12_out), .out(multiplexer_10_out), .sel(not_3_out));
  Multiplexer #(.select(1), .width(1), .disabled("Z"), .enable("false")) multiplexer_11 (
    .in0(RegWrite), .in1(ExRegWrite), .out(multiplexer_11_out), .sel(IsCOP0));
  RegFile regfile_1 (
    .R1_num(multiplexer_7_out), .R2_num(multiplexer_8_out), .RW(multiplexer_9_out),
    .in_4(multiplexer_10_out), .WE(multiplexer_11_out), .clk(clk), .R1(regfile_1_r1), .R2(regfile_1_r2));
  assign bit_extender_1_out = {{27{1'b0}}, multiplexer_5_out[10:6]};  // Bit_Extender bit_extender_1
  ImmeExtend immeextend_1 (.in_1(multiplexer_5_out[15:0]), .zeroExtend(ZeroExtend), .out_3(immeextend_1_out_3));
  not not_4 (not_4_out, IsJAL);
  Multiplexer #(.select(1), .width(32), .disabled("Z"), .enable("false")) multiplexer_12 (
    .in0(adder_1_out), .in1(multiplexer_19_out), .out(multiplexer_12_out), .sel(not_4_out));
  Shifter #(.width(32), .shift("ll")) shifter_1 (.in(immeextend_1_out_3), .\dist (5'b00010), .out(shifter_1_out));
  Cop0 cop0_1 (
    .ExpSrc0(exp0), .ExpSrc1(_1), .ExpSrc2(_2), .clk(clk), .enable(IsCOP0), .Inst(multiplexer_5_out),
    .PCin(register_1_q), .Din(regfile_1_r2), .ExRegWrite(ExRegWrite), .ExpBlock(ExpBlock), .IsEret(IsEret),
    .HasExp(HasExp), .PCout(cop0_1_pcout), .Dout(cop0_1_dout));
  xor xor_1 (xor_1_out, Equal, BneOrBeq);
  Adder #(.width(32)) adder_3 (
    .a(shifter_1_out), .b({adder_2_out, adder_2_out_2}), .out(adder_3_out));  // open: cin, cout
  SyscallDecoder syscalldecoder_1 (
    .clk(clk), .Enable(IsSyscall), .v0(regfile_1_r1), .a0(regfile_1_r2), .out_5(Halt),
    .out_6({syscalldecoder_1_out_6_4, syscalldecoder_1_out_6_3, syscalldecoder_1_out_6_2, syscalldecoder_1_out_6}));
  Multiplexer #(.select(1), .width(32), .disabled("Z"), .enable("false")) multiplexer_13 (
    .in0(regfile_1_r2), .in1(immeextend_1_out_3), .out(multiplexer_13_out), .sel(ALUSrc));
  Multiplexer #(.select(1), .width(32), .disabled("Z"), .enable("false")) multiplexer_14 (
    .in0({adder_2_out, adder_2_out_2}), .in1(adder_3_out), .out(multiplexer_14_out), .sel(and_2_out));
  not not_5 (not_5_out, Jump);
  Hex_Digit_Display hex_digit_display_1 (.value(syscalldecoder_1_out_6_4));  // open: dp
  Multiplexer #(.select(1), .width(32), .disabled("Z"), .enable("false")) multiplexer_15 (
    .in0(regfile_1_r1), .in1(regfile_1_r2), .out(multiplexer_15_out), .sel(IsShamt));
  Multiplexer #(.select(1), .width(32), .disabled("Z"), .enable("false")) multiplexer_16 (
    .in0(multiplexer_13_out), .in1(bit_extender_1_out), .out(multiplexer_16_out), .sel(IsShamt));
  and and_2 (and_2_out, Branch, xor_1_out);
  Multiplexer #(.select(1), .width(32), .disabled("Z"), .enable("false")) multiplexer_17 (
    .in0({adder_2_out, multiplexer_5_out[25:0], 2'b00}), .in1(multiplexer_14_out), .out(multiplexer_17_out),
    .sel(not_5_out));
  Hex_Digit_Display hex_digit_display_2 (.value(syscalldecoder_1_out_6_2));  // open: dp
  Hex_Digit_Display hex_digit_display_3 (.value(syscalldecoder_1_out_6_3));  // open: dp
  ALU alu_1 (
    .X(multiplexer_15_out), .Y(multiplexer_16_out), .in_3(ALOop), .Result1(alu_1_result1), .Equal(Equal));  // open: Result2, OF, CF
  Hex_Digit_Display hex_digit_display_4 (.value(syscalldecoder_1_out_6[15:12]));  // open: dp
  Hex_Digit_Display hex_digit_display_5 (.value(syscalldecoder_1_out_6[19:16]));  // open: dp
  Hex_Digit_Display hex_digit_display_6 (.value(syscalldecoder_1_out_6[11:8]));  // open: dp
  Hex_Digit_Display hex_digit_display_7 (.value(syscalldecoder_1_out_6[7:4]));  // open: dp
  Multiplexer #(.select(1), .width(32), .disabled("Z"), .enable("false")) multiplexer_18 (
    .in0(multiplexer_17_out), .in1(regfile_1_r1), .out(multiplexer_18_out), .sel(IsJR));
  Hex_Digit_Display hex_digit_display_8 (.value(syscalldecoder_1_out_6[3:0]));  // open: dp
  RAM #(.addrWidth(10), .dataWidth(32), .bus("separate"), .Select("low")) ram_1 (
    .addr(alu_1_result1[11:2]), .din(regfile_1_r2), .data(ram_1_data), .str(MemWrite), .clk(clk), .ld(MemRead));  // open: sel, clr
  Multiplexer #(.select(1), .width(32), .disabled("Z"), .enable("false")) multiplexer_19 (
    .in0(alu_1_result1), .in1(ram_1_data), .out(multiplexer_19_out), .sel(MemtoReg));

  // Notes on the sheet:
  //   contents of rom_1 (hex, n*v repeats v):
  //   20110001 8000c05 20110001 20120002 20130003 8000c09 20110001 20120002 20130003 8000c0d 20110001
  //   20120002 20130003 8000c11 20110001 20120002 20130003 c000d2e 20100001 20110001 118fc0 112020
  //   20020022 c 118882 12200001 8000c15 112020 20020022 c 20110001 118880 112020 20020022 c 12200001
  //   8000c1f 20110001 118fc0 112020 20020022 c 1188c3 112020 20020022 c 118903 112020 20020022 c 118903
  //   112020 20020022 c 118903 112020 20020022 c 118903 112020 20020022 c 118903 112020 20020022 c 118903
  //   112020 20020022 c 118903 112020 20020022 c 20100001 109fc0 139fc3 8021 2012000c 24160003 26100001
  //   3210000f 20080008 20090001 139900 2709825 132020 20020022 c 1094022 1500fff9 22100001 2018000f
  //   2188024 108700 20080008 20090001 139902 2709825 132021 20020022 c 1094022 1500fff9 108702 2c9b022
  //   12c00001 8000c50 4020 1084027 84400 3508ffff 82021 20020022 c 20110004 ae310000 8e320000 2252fffc
  //   20100000 22110001 2118020 22520004 ae500000 22310001 2118020 22520004 ae500000 22310001 2118020
  //   22520004 ae500000 22310001 2118020 22520004 ae500000 22310001 2118020 22520004 ae500000 22310001
  //   2118020 22520004 ae500000 22310001 2118020 22520004 ae500000 20090001 8c080004 1509008f ac000004
  //   20090003 8c080008 1509008b ac000008 20090006 8c08000c 15090087 ac00000c 2009000a 8c080010 15090083
  //   ac000010 2009000f 8c080014 1509007f ac000014 20090015 8c080018 1509007b ac000018 2009001c 8c08001c
  //   15090077 ac00001c 2010ffff 20110000 ae300000 22100001 22310004 ae300000 22100001 22310004 ae300000
  //   22100001 22310004 ae300000 22100001 22310004 ae300000 22100001 22310004 ae300000 22100001 22310004
  //   ae300000 22100001 22310004 ae300000 22100001 22310004 ae300000 22100001 22310004 ae300000 22100001
  //   22310004 ae300000 22100001 22310004 ae300000 22100001 22310004 ae300000 22100001 22310004 ae300000
  //   22100001 22310004 ae300000 22100001 22310004 ae300000 22100001 22310004 22100001 8020 2011003c
  //   8e130000 8e340000 274402a 11000002 ae330000 ae140000 2231fffc 1611fff8 102020 20020022 c 22100004
  //   2011003c 1611fff2 20100001 201200ff 20110001 20130003 12120005 12100004 20110001 20120002 20130003
  //   8000d26 102020 20020001 c 16310005 16320004 20110001 20120002 20130003 8000d26 132020 20020001 c
  //   2011ffff 118c00 2020 24840064 2484ff9c 14800017 2020 2484ff9c 24840064 14800013 2020 34847fff 912024
  //   1480000f 2020 34848000 912024 1480000b 24040000 8000d20 8000d26 2002000a c 20041ced 42400 3484cafe
  //   20020022 c 8000d1e 3c010000 3421baad 12020 42400 3484c0de 20020022 c 8000d1e 20100000 22100001
  //   102020 20020022 c 22100002 102020 20020022 c 22100003 102020 20020022 c 22100004 102020 20020022 c
  //   22100005 102020 20020022 c 22100006 102020 20020022 c 22100007 102020 20020022 c 22100008 102020
  //   20020022 c 3e00008
  //   contents of rom_2 (hex, n*v repeats v):
  //   201a0001 409a0800 201c0400 39df020 401a0000 afda0000 23de0004 23bd0004 401b1000 401a1800 409a1000
  //   afd00000 23bd0004 23de0004 afd40000 23bd0004 23de0004 afd50000 23bd0004 23de0004 afd60000 23bd0004
  //   23de0004 afc40000 23bd0004 23de0004 afc20000 23bd0004 23de0004 afdb0000 23bd0004 23de0004 1ab020
  //   22d60001 201a0000 409a0800 20140005 20150001 168020 102020 20020022 c 108100 1600fffb 295a022
  //   1680fff8 201a0001 409a0800 23defffc 23bdfffc 8fdb0000 23defffc 23bdfffc 8fc20000 23defffc 23bdfffc
  //   8fc40000 23defffc 23bdfffc 8fd60000 23defffc 23bdfffc 8fd50000 23defffc 23bdfffc 8fd40000 23defffc
  //   23bdfffc 8fd00000 409b1000 23defffc 23bdfffc 8fda0000 409a0000 201a0000 409a0800 42000018
endmodule

module ALU (
  input  [31:0] X,
  input  [31:0] Y,
  input  [3:0] in_3,
  output [31:0] Result1,
  output [31:0] Result2,
  output OF,
  output CF,
  output Equal
);

  wire comparator_1_lt, comparator_2_lt;
  wire [1:0] adderwithoverflow_1_cf, subtractorwithoverflow_1_cf;
  wire [31:0] adderwithoverflow_1_result, and_1_out, bit_extender_1_out, bit_extender_2_out, divider_1_out,
       divider_1_rem, multiplier_1_cout, multiplier_1_out, not_1_out, or_1_out, or_2_out, shifter_1_out,
       shifter_2_out, shifter_3_out, subtractorwithoverflow_1_result, xor_1_out;

  Shifter #(.width(32), .shift("ll")) shifter_1 (.in(X), .\dist (Y[4:0]), .out(shifter_1_out));
  Shifter #(.width(32), .shift("ar")) shifter_2 (.in(X), .\dist (Y[4:0]), .out(shifter_2_out));
  Shifter #(.width(32), .shift("lr")) shifter_3 (.in(X), .\dist (Y[4:0]), .out(shifter_3_out));
  Multiplier #(.width(32)) multiplier_1 (.a(X), .b(Y), .out(multiplier_1_out), .cout(multiplier_1_cout));  // open: cin
  Divider #(.width(32)) divider_1 (.a(X), .b(Y), .out(divider_1_out), .rem(divider_1_rem));  // open: upper
  Multiplexer #(.select(4), .width(2), .disabled("Z"), .enable("false")) multiplexer_1 (
    .in0(2'b00), .in1(2'b00), .in2(2'b00), .in3(2'b00), .in4(2'b00), .in5(adderwithoverflow_1_cf),
    .in6(subtractorwithoverflow_1_cf), .in7(2'b00), .in8(2'b00), .in9(2'b00), .in10(2'b00), .in11(2'b00),
    .in12(2'b00), .in13(2'b00), .in14(2'b00), .in15(2'b00), .out({OF, CF}), .sel(in_3));
  AdderWithOverFlow adderwithoverflow_1 (
    .in_1(X), .in_2(Y), .Result(adderwithoverflow_1_result), .CF(adderwithoverflow_1_cf[0]),
    .OF(adderwithoverflow_1_cf[1]));  // open: cin
  Multiplexer #(.select(4), .width(32), .disabled("Z"), .enable("false")) multiplexer_2 (
    .in0(shifter_1_out), .in1(shifter_2_out), .in2(shifter_3_out), .in3(multiplier_1_out),
    .in4(divider_1_out), .in5(adderwithoverflow_1_result), .in6(subtractorwithoverflow_1_result),
    .in7(and_1_out), .in8(or_1_out), .in9(xor_1_out), .in10(not_1_out), .in11(bit_extender_1_out),
    .in12(bit_extender_2_out), .in13({32{1'b0}}), .in14({32{1'b0}}), .in15({32{1'b0}}), .out(Result1),
    .sel(in_3));
  SubtractorWithOverFlow subtractorwithoverflow_1 (
    .in_1(X), .in_2(Y), .Result(subtractorwithoverflow_1_result), .CF(subtractorwithoverflow_1_cf[0]),
    .OF(subtractorwithoverflow_1_cf[1]));  // open: bin
  assign and_1_out = X & Y;  // AND_Gate and_1, 32 bits wide
  assign or_1_out = X | Y;  // OR_Gate or_1, 32 bits wide
  Multiplexer #(.select(4), .width(32), .disabled("Z"), .enable("false")) multiplexer_3 (
    .in0({32{1'b0}}), .in1({32{1'b0}}), .in2({32{1'b0}}), .in3(multiplier_1_cout), .in4(divider_1_rem),
    .in5({32{1'b0}}), .in6({32{1'b0}}), .in7({32{1'b0}}), .in8({32{1'b0}}), .in9({32{1'b0}}),
    .in10({32{1'b0}}), .in11({32{1'b0}}), .in12({32{1'b0}}), .in13({32{1'b0}}), .in14({32{1'b0}}),
    .in15({32{1'b0}}), .out(Result2), .sel(in_3));
  assign xor_1_out = X ^ Y;  // XOR_Gate xor_1, 32 bits wide
  assign or_2_out = X | Y;  // OR_Gate or_2, 32 bits wide
  assign not_1_out = ~or_2_out;  // NOT_Gate not_1, 32 bits wide
  Comparator #(.width(32), .mode("twosComplement")) comparator_1 (.a(X), .b(Y), .lt(comparator_1_lt));  // open: gt, eq
  assign bit_extender_1_out = {{31{1'b0}}, comparator_1_lt};  // Bit_Extender bit_extender_1
  Comparator #(.width(32), .mode("twosComplement")) comparator_2 (
    .a(X), .b(Y), .eq(Equal), .lt(comparator_2_lt));  // open: gt
  assign bit_extender_2_out = {{31{1'b0}}, comparator_2_lt};  // Bit_Extender bit_extender_2

  // Other names for the same wires on the sheet: AluOP[3:0] = in_3
endmodule

// +
module AdderWithOverFlow (
  input  [31:0] in_1,
  input  [31:0] in_2,
  input  cin,
  output [31:0] Result,
  output CF,
  output OF
);

  wire adder_1_cout;

  Adder #(.width(31)) adder_1 (.a(in_1[30:0]), .b(in_2[30:0]), .out(Result[30:0]), .cin(cin), .cout(adder_1_cout));
  Adder #(.width(1)) adder_2 (.a(in_1[31]), .b(in_2[31]), .out(Result[31]), .cin(adder_1_cout), .cout(CF));
  xor xor_1 (OF, adder_1_cout, CF);

  // Other names for the same wires on the sheet: X[31:0] = in_1; Y[31:0] = in_2
endmodule

// -
module SubtractorWithOverFlow (
  input  [31:0] in_1,
  input  [31:0] in_2,
  input  bin,
  output [31:0] Result,
  output CF,
  output OF
);

  wire subtractor_1_bout;

  Subtractor #(.width(31)) subtractor_1 (
    .a(in_1[30:0]), .b(in_2[30:0]), .out(Result[30:0]), .bin(bin), .bout(subtractor_1_bout));
  Subtractor #(.width(1)) subtractor_2 (
    .a(in_1[31]), .b(in_2[31]), .out(Result[31]), .bin(subtractor_1_bout), .bout(CF));
  xor xor_1 (OF, subtractor_1_bout, CF);

  // Other names for the same wires on the sheet: X[31:0] = in_1; Y[31:0] = in_2
endmodule

module RegFile (
  input  [4:0] R1_num,
  input  [4:0] R2_num,
  input  [4:0] RW,
  input  [31:0] in_4,
  input  WE,
  input  clk,
  output [31:0] R1,
  output [31:0] R2
);

  wire demultiplexer_1_out0, demultiplexer_1_out1, demultiplexer_1_out2, demultiplexer_1_out3,
       demultiplexer_2_out0, demultiplexer_2_out1, demultiplexer_2_out2, demultiplexer_2_out3,
       demultiplexer_2_out4, demultiplexer_2_out5, demultiplexer_2_out6, demultiplexer_2_out7,
       demultiplexer_3_out0, demultiplexer_3_out1, demultiplexer_3_out2, demultiplexer_3_out3,
       demultiplexer_3_out4, demultiplexer_3_out5, demultiplexer_3_out6, demultiplexer_3_out7,
       demultiplexer_4_out0, demultiplexer_4_out1, demultiplexer_4_out2, demultiplexer_4_out3,
       demultiplexer_4_out4, demultiplexer_4_out5, demultiplexer_4_out6, demultiplexer_4_out7,
       demultiplexer_5_out0, demultiplexer_5_out1, demultiplexer_5_out2, demultiplexer_5_out3,
       demultiplexer_5_out4, demultiplexer_5_out5, demultiplexer_5_out6, demultiplexer_5_out7;
  wire [31:0] a0_q, a1_q, a2_q, a3_q, at_q, fp_q, gp_q, k0_q, k1_q, ra_q, s0_q, s1_q, s2_q, s3_q, s4_q, s5_q,
       s6_q, s7_q, sp_q, t0_q, t1_q, t2_q, t3_q, t4_q, t5_q, t6_q, t7_q, t8_q, t9_q, v0_q, v1_q, Zero_q;

  Demultiplexer #(.select(2), .width(1), .tristate("false"), .disabled(0), .enable("true")) demultiplexer_1 (
    .out0(demultiplexer_1_out0), .out1(demultiplexer_1_out1), .out2(demultiplexer_1_out2),
    .out3(demultiplexer_1_out3), .in(1'b1), .sel(RW[4:3]), .en(WE));
  Demultiplexer #(.select(3), .width(1), .tristate("false"), .disabled(0), .enable("true")) demultiplexer_2 (
    .out0(demultiplexer_2_out0), .out1(demultiplexer_2_out1), .out2(demultiplexer_2_out2),
    .out3(demultiplexer_2_out3), .out4(demultiplexer_2_out4), .out5(demultiplexer_2_out5),
    .out6(demultiplexer_2_out6), .out7(demultiplexer_2_out7), .in(1'b1), .sel(RW[2:0]),
    .en(demultiplexer_1_out0));
  Demultiplexer #(.select(3), .width(1), .tristate("false"), .disabled(0), .enable("true")) demultiplexer_3 (
    .out0(demultiplexer_3_out0), .out1(demultiplexer_3_out1), .out2(demultiplexer_3_out2),
    .out3(demultiplexer_3_out3), .out4(demultiplexer_3_out4), .out5(demultiplexer_3_out5),
    .out6(demultiplexer_3_out6), .out7(demultiplexer_3_out7), .in(1'b1), .sel(RW[2:0]),
    .en(demultiplexer_1_out1));
  Demultiplexer #(.select(3), .width(1), .tristate("false"), .disabled(0), .enable("true")) demultiplexer_4 (
    .out0(demultiplexer_4_out0), .out1(demultiplexer_4_out1), .out2(demultiplexer_4_out2),
    .out3(demultiplexer_4_out3), .out4(demultiplexer_4_out4), .out5(demultiplexer_4_out5),
    .out6(demultiplexer_4_out6), .out7(demultiplexer_4_out7), .in(1'b1), .sel(RW[2:0]),
    .en(demultiplexer_1_out2));
  Demultiplexer #(.select(3), .width(1), .tristate("false"), .disabled(0), .enable("true")) demultiplexer_5 (
    .out0(demultiplexer_5_out0), .out1(demultiplexer_5_out1), .out2(demultiplexer_5_out2),
    .out3(demultiplexer_5_out3), .out4(demultiplexer_5_out4), .out5(demultiplexer_5_out5),
    .out6(demultiplexer_5_out6), .out7(demultiplexer_5_out7), .in(1'b1), .sel(RW[2:0]),
    .en(demultiplexer_1_out3));
  Register #(.width(32), .trigger("rising"), .Select("low")) Zero (
    .D(in_4), .en(demultiplexer_2_out0), .Q(Zero_q));  // open: clk, clr
  Register #(.width(32), .trigger("rising"), .Select("low")) t0 (
    .D(in_4), .en(demultiplexer_3_out0), .Q(t0_q), .clk(clk));  // open: clr
  Register #(.width(32), .trigger("rising"), .Select("low")) s0 (
    .D(in_4), .en(demultiplexer_4_out0), .Q(s0_q), .clk(clk));  // open: clr
  Register #(.width(32), .trigger("rising"), .Select("low")) t8 (
    .D(in_4), .en(demultiplexer_5_out0), .Q(t8_q), .clk(clk));  // open: clr
  Register #(.width(32), .trigger("rising"), .Select("low")) at (
    .D(in_4), .en(demultiplexer_2_out1), .Q(at_q), .clk(clk));  // open: clr
  Register #(.width(32), .trigger("rising"), .Select("low")) t1 (
    .D(in_4), .en(demultiplexer_3_out1), .Q(t1_q), .clk(clk));  // open: clr
  Register #(.width(32), .trigger("rising"), .Select("low")) s1 (
    .D(in_4), .en(demultiplexer_4_out1), .Q(s1_q), .clk(clk));  // open: clr
  Register #(.width(32), .trigger("rising"), .Select("low")) t9 (
    .D(in_4), .en(demultiplexer_5_out1), .Q(t9_q), .clk(clk));  // open: clr
  Register #(.width(32), .trigger("rising"), .Select("low")) v0 (
    .D(in_4), .en(demultiplexer_2_out2), .Q(v0_q), .clk(clk));  // open: clr
  Register #(.width(32), .trigger("rising"), .Select("low")) t2 (
    .D(in_4), .en(demultiplexer_3_out2), .Q(t2_q), .clk(clk));  // open: clr
  Register #(.width(32), .trigger("rising"), .Select("low")) s2 (
    .D(in_4), .en(demultiplexer_4_out2), .Q(s2_q), .clk(clk));  // open: clr
  Register #(.width(32), .trigger("rising"), .Select("low")) k0 (
    .D(in_4), .en(demultiplexer_5_out2), .Q(k0_q), .clk(clk));  // open: clr
  Register #(.width(32), .trigger("rising"), .Select("low")) v1 (
    .D(in_4), .en(demultiplexer_2_out3), .Q(v1_q), .clk(clk));  // open: clr
  Register #(.width(32), .trigger("rising"), .Select("low")) t3 (
    .D(in_4), .en(demultiplexer_3_out3), .Q(t3_q), .clk(clk));  // open: clr
  Register #(.width(32), .trigger("rising"), .Select("low")) s3 (
    .D(in_4), .en(demultiplexer_4_out3), .Q(s3_q), .clk(clk));  // open: clr
  Register #(.width(32), .trigger("rising"), .Select("low")) k1 (
    .D(in_4), .en(demultiplexer_5_out3), .Q(k1_q), .clk(clk));  // open: clr
  Register #(.width(32), .trigger("rising"), .Select("low")) a0 (
    .D(in_4), .en(demultiplexer_2_out4), .Q(a0_q), .clk(clk));  // open: clr
  Register #(.width(32), .trigger("rising"), .Select("low")) t4 (
    .D(in_4), .en(demultiplexer_3_out4), .Q(t4_q), .clk(clk));  // open: clr
  Register #(.width(32), .trigger("rising"), .Select("low")) s4 (
    .D(in_4), .en(demultiplexer_4_out4), .Q(s4_q), .clk(clk));  // open: clr
  Register #(.width(32), .trigger("rising"), .Select("low")) gp (
    .D(in_4), .en(demultiplexer_5_out4), .Q(gp_q), .clk(clk));  // open: clr
  Register #(.width(32), .trigger("rising"), .Select("low")) a1 (
    .D(in_4), .en(demultiplexer_2_out5), .Q(a1_q), .clk(clk));  // open: clr
  Register #(.width(32), .trigger("rising"), .Select("low")) t5 (
    .D(in_4), .en(demultiplexer_3_out5), .Q(t5_q), .clk(clk));  // open: clr
  Register #(.width(32), .trigger("rising"), .Select("low")) s5 (
    .D(in_4), .en(demultiplexer_4_out5), .Q(s5_q), .clk(clk));  // open: clr
  Register #(.width(32), .trigger("rising"), .Select("low")) sp (
    .D(in_4), .en(demultiplexer_5_out5), .Q(sp_q), .clk(clk));  // open: clr
  Register #(.width(32), .trigger("rising"), .Select("low")) a2 (
    .D(in_4), .en(demultiplexer_2_out6), .Q(a2_q), .clk(clk));  // open: clr
  Register #(.width(32), .trigger("rising"), .Select("low")) t6 (
    .D(in_4), .en(demultiplexer_3_out6), .Q(t6_q), .clk(clk));  // open: clr
  Register #(.width(32), .trigger("rising"), .Select("low")) s6 (
    .D(in_4), .en(demultiplexer_4_out6), .Q(s6_q), .clk(clk));  // open: clr
  Register #(.width(32), .trigger("rising"), .Select("low")) fp (
    .D(in_4), .en(demultiplexer_5_out6), .Q(fp_q), .clk(clk));  // open: clr
  Register #(.width(32), .trigger("rising"), .Select("low")) a3 (
    .D(in_4), .en(demultiplexer_2_out7), .Q(a3_q), .clk(clk));  // open: clr
  Register #(.width(32), .trigger("rising"), .Select("low")) t7 (
    .D(in_4), .en(demultiplexer_3_out7), .Q(t7_q), .clk(clk));  // open: clr
  Register #(.width(32), .trigger("rising"), .Select("low")) s7 (
    .D(in_4), .en(demultiplexer_4_out7), .Q(s7_q), .clk(clk));  // open: clr
  Register #(.width(32), .trigger("rising"), .Select("low")) ra (
    .D(in_4), .en(demultiplexer_5_out7), .Q(ra_q), .clk(clk));  // open: clr
  Multiplexer #(.select(5), .width(32), .disabled("Z"), .enable("false")) multiplexer_1 (
    .in0(Zero_q), .in1(at_q), .in2(v0_q), .in3(v1_q), .in4(a0_q), .in5(a1_q), .in6(a2_q), .in7(a3_q),
    .in8(t0_q), .in9(t1_q), .in10(t2_q), .in11(t3_q), .in12(t4_q), .in13(t5_q), .in14(t6_q), .in15(t7_q),
    .in16(s0_q), .in17(s1_q), .in18(s2_q), .in19(s3_q), .in20(s4_q), .in21(s5_q), .in22(s6_q), .in23(s7_q),
    .in24(t8_q), .in25(t9_q), .in26(k0_q), .in27(k1_q), .in28(gp_q), .in29(sp_q), .in30(fp_q), .in31(ra_q),
    .out(R1), .sel(R1_num));
  Multiplexer #(.select(5), .width(32), .disabled("Z"), .enable("false")) multiplexer_2 (
    .in0(Zero_q), .in1(at_q), .in2(v0_q), .in3(v1_q), .in4(a0_q), .in5(a1_q), .in6(a2_q), .in7(a3_q),
    .in8(t0_q), .in9(t1_q), .in10(t2_q), .in11(t3_q), .in12(t4_q), .in13(t5_q), .in14(t6_q), .in15(t7_q),
    .in16(s0_q), .in17(s1_q), .in18(s2_q), .in19(s3_q), .in20(s4_q), .in21(s5_q), .in22(s6_q), .in23(s7_q),
    .in24(t8_q), .in25(t9_q), .in26(k0_q), .in27(k1_q), .in28(gp_q), .in29(sp_q), .in30(fp_q), .in31(ra_q),
    .out(R2), .sel(R2_num));

  // Other names for the same wires on the sheet: reg1[31:0] = R1; reg1_num[4:0] = R1_num; reg2[31:0] = R2;
  //   reg2_num[4:0] = R2_num; write_data[31:0] = in_4; write_reg_num[4:0] = RW
endmodule

module SyscallDecoder (
  input  clk,
  input  Enable,
  input  [31:0] v0,
  input  [31:0] a0,
  output out_5,
  output [31:0] out_6
);

  wire comparator_1_eq;

  Comparator #(.width(32), .mode("twosComplement")) comparator_1 (
    .a(v0), .b(32'ha), .eq(comparator_1_eq));  // open: gt, lt
  Register #(.width(32), .trigger("rising"), .Select("low")) register_1 (
    .D(a0), .en(Enable), .Q(out_6), .clk(clk));  // open: clr
  Multiplexer #(.select(1), .width(1), .disabled("Z"), .enable("false")) multiplexer_1 (
    .in0(1'b0), .in1(comparator_1_eq), .out(out_5), .sel(Enable));

  // Other names for the same wires on the sheet: Halt = out_5; Hex[31:0] = out_6
endmodule

module Control (
  input  [5:0] op,
  input  [5:0] Funct,
  output IsJAL,
  output IsShamt,
  output MemtoReg,
  output RegWrite,
  output BneOrBeq,
  output ALUSrc,
  output IsSyscal,
  output ZeroExtend,
  output MemRead,
  output MemWrite,
  output Jump,
  output Branch,
  output RegDst,
  output IsJR,
  output IsCOP0,
  output [3:0] out_18
);

  wire and_3_out, and_4_out, and_5_out, and_6_out, and_7_out, and_8_out, and_9_out, and_10_out, and_12_out,
       and_13_out, and_14_out, and_15_out, and_16_out, and_17_out, and_18_out, and_19_out, and_20_out,
       and_21_out, and_22_out, and_23_out, and_24_out, and_25_out, and_30_out, and_31_out, and_33_out,
       and_34_out, and_35_out, and_36_out, and_37_out, and_38_out, and_39_out, and_40_out, and_41_out,
       and_42_out, and_43_out, and_44_out, and_45_out, and_46_out, and_47_out, and_48_out, and_49_out,
       and_50_out, and_51_out, and_52_out, and_53_out, and_54_out, and_55_out, and_56_out, and_57_out,
       and_58_out, and_59_out, and_60_out, and_61_out, and_62_out, and_63_out, and_64_out, and_65_out,
       and_66_out, and_67_out, and_68_out, and_69_out, and_70_out, and_71_out, and_72_out, and_73_out,
       and_74_out, and_75_out, and_76_out, and_77_out, and_78_out, and_79_out, and_80_out, and_81_out,
       IsSpecial, not_1_out, or_9_out;
  wire [3:0] or_10_out, or_14_out;

  and and_1 (MemRead, op[5], ~op[4], ~op[3], ~op[2], op[1], op[0]);  // AND_Gate
  and and_2 (MemWrite, op[5], ~op[4], op[3], ~op[2], op[1], op[0]);  // AND_Gate
  and and_3 (and_3_out, ~op[5], ~op[4], op[3], ~op[2], ~op[1], ~op[0]);  // AND_Gate
  and and_4 (and_4_out, op[5], ~op[4], ~op[3], ~op[2], op[1], op[0]);  // AND_Gate
  and and_5 (and_5_out, op[5], ~op[4], op[3], ~op[2], op[1], op[0]);  // AND_Gate
  and and_6 (and_6_out, ~op[5], ~op[4], op[3], op[2], ~op[1], ~op[0]);  // AND_Gate
  and and_7 (and_7_out, ~op[5], ~op[4], op[3], op[2], ~op[1], op[0]);  // AND_Gate
  and and_8 (and_8_out, ~op[5], ~op[4], op[3], ~op[2], op[1], ~op[0]);  // AND_Gate
  and and_9 (and_9_out, ~op[5], ~op[4], op[3], ~op[2], ~op[1], op[0]);  // AND_Gate
  and and_10 (and_10_out, ~op[5], ~op[4], op[3], ~op[2], ~op[1], ~op[0]);  // AND_Gate
  or or_1 (ALUSrc, and_3_out, and_4_out, and_5_out, and_6_out, and_7_out, and_8_out, and_9_out, and_10_out);
  and and_11 (MemtoReg, op[5], ~op[4], ~op[3], ~op[2], op[1], op[0]);  // AND_Gate
  and and_12 (and_12_out, ~op[5], ~op[4], ~op[3], ~op[2], op[1], ~op[0]);  // AND_Gate
  and and_13 (and_13_out, ~op[5], ~op[4], ~op[3], ~op[2], op[1], op[0]);  // AND_Gate
  or or_2 (Jump, and_12_out, and_13_out);
  and and_14 (and_14_out, ~op[5], ~op[4], ~op[3], op[2], ~op[1], op[0]);  // AND_Gate
  and and_15 (and_15_out, ~op[5], ~op[4], ~op[3], op[2], ~op[1], ~op[0]);  // AND_Gate
  or or_3 (Branch, and_14_out, and_15_out);
  and and_16 (and_16_out, ~op[5], ~op[4], ~op[3], ~op[2], ~op[1], ~op[0]);  // AND_Gate
  and and_17 (and_17_out, ~op[5], ~op[4], op[3], ~op[2], ~op[1], ~op[0]);  // AND_Gate
  and and_18 (and_18_out, op[5], ~op[4], ~op[3], ~op[2], op[1], op[0]);  // AND_Gate
  and and_19 (and_19_out, ~op[5], ~op[4], op[3], op[2], ~op[1], ~op[0]);  // AND_Gate
  and and_20 (and_20_out, ~op[5], ~op[4], op[3], op[2], ~op[1], op[0]);  // AND_Gate
  and and_21 (and_21_out, ~op[5], ~op[4], op[3], ~op[2], op[1], ~op[0]);  // AND_Gate
  and and_22 (and_22_out, ~op[5], ~op[4], op[3], ~op[2], ~op[1], op[0]);  // AND_Gate
  and and_23 (and_23_out, ~op[5], ~op[4], op[3], ~op[2], ~op[1], ~op[0]);  // AND_Gate
  and and_24 (and_24_out, ~op[5], ~op[4], ~op[3], ~op[2], op[1], op[0]);  // AND_Gate
  and and_25 (and_25_out, ~op[5], op[4], ~op[3], ~op[2], ~op[1], ~op[0]);  // AND_Gate
  and and_26 (RegDst, ~op[5], ~op[4], ~op[3], ~op[2], ~op[1], ~op[0]);  // AND_Gate
  or or_4 (RegWrite, and_16_out, and_17_out, and_18_out, and_19_out, and_20_out, and_21_out, and_22_out, and_23_out, and_24_out, and_25_out);
  and and_27 (BneOrBeq, ~op[5], ~op[4], ~op[3], op[2], ~op[1], op[0]);  // AND_Gate
  and and_28 (IsJAL, ~op[5], ~op[4], ~op[3], ~op[2], op[1], op[0]);  // AND_Gate
  and and_29 (IsCOP0, ~op[5], op[4], ~op[3], ~op[2], ~op[1], ~op[0]);  // AND_Gate
  and and_30 (and_30_out, ~op[5], ~op[4], op[3], op[2], ~op[1]);  // AND_Gate
  and and_31 (and_31_out, ~op[5], ~op[4], op[3], op[2], op[1], ~op[0]);  // AND_Gate
  or or_5 (ZeroExtend, and_30_out, and_31_out);
  and and_32 (IsSpecial, ~op[5], ~op[4], ~op[3], ~op[2], ~op[1], ~op[0]);  // AND_Gate
  and and_33 (and_33_out, ~op[5], ~op[4], op[3], op[2], ~op[1], op[0]);  // AND_Gate
  and and_34 (and_34_out, ~op[5], ~op[4], op[3], ~op[2], op[1], ~op[0]);  // AND_Gate
  and and_35 (and_35_out, ~op[5], ~op[4], ~op[3], ~op[2], ~op[1], ~op[0]);  // AND_Gate
  and and_36 (and_36_out, ~op[5], ~op[4], op[3], ~op[2], ~op[1], ~op[0]);  // AND_Gate
  and and_37 (and_37_out, op[5], ~op[4], ~op[3], ~op[2], op[1], op[0]);  // AND_Gate
  and and_38 (and_38_out, op[5], ~op[4], op[3], ~op[2], op[1], op[0]);  // AND_Gate
  and and_39 (and_39_out, ~op[5], ~op[4], ~op[3], op[2], ~op[1], op[0]);  // AND_Gate
  and and_40 (and_40_out, ~op[5], ~op[4], ~op[3], op[2], ~op[1], ~op[0]);  // AND_Gate
  and and_41 (and_41_out, ~op[5], ~op[4], op[3], op[2], ~op[1], ~op[0]);  // AND_Gate
  and and_42 (and_42_out, ~op[5], ~op[4], op[3], ~op[2], ~op[1], op[0]);  // AND_Gate
  and and_43 (and_43_out, ~op[5], ~op[4], ~op[3], ~op[2], op[1], ~op[0]);  // AND_Gate
  and and_44 (and_44_out, ~op[5], ~op[4], ~op[3], ~op[2], op[1], op[0]);  // AND_Gate
  and and_45 (and_45_out, ~op[5], op[4], ~op[3], ~op[2], ~op[1], ~op[0]);  // AND_Gate
  and and_46 (and_46_out, ~op[5], ~op[4], op[3], op[2], ~op[1], ~op[0]);  // AND_Gate
  and and_47 (and_47_out, ~op[5], ~op[4], op[3], ~op[2], op[1], ~op[0]);  // AND_Gate
  and and_48 (and_48_out, ~op[5], ~op[4], ~op[3], ~op[2], ~op[1], ~op[0]);  // AND_Gate
  and and_49 (and_49_out, ~op[5], ~op[4], op[3], ~op[2], ~op[1], ~op[0]);  // AND_Gate
  and and_50 (and_50_out, op[5], ~op[4], op[3], ~op[2], op[1], op[0]);  // AND_Gate
  and and_51 (and_51_out, ~op[5], ~op[4], ~op[3], op[2], ~op[1], op[0]);  // AND_Gate
  and and_52 (and_52_out, ~op[5], ~op[4], ~op[3], op[2], ~op[1], ~op[0]);  // AND_Gate
  and and_53 (and_53_out, ~op[5], ~op[4], op[3], op[2], ~op[1], ~op[0]);  // AND_Gate
  and and_54 (and_54_out, ~op[5], ~op[4], op[3], ~op[2], op[1], ~op[0]);  // AND_Gate
  and and_55 (and_55_out, ~op[5], ~op[4], op[3], ~op[2], ~op[1], op[0]);  // AND_Gate
  and and_56 (and_56_out, ~op[5], ~op[4], ~op[3], ~op[2], op[1], ~op[0]);  // AND_Gate
  and and_57 (and_57_out, ~op[5], ~op[4], ~op[3], ~op[2], op[1], op[0]);  // AND_Gate
  and and_58 (and_58_out, ~op[5], op[4], ~op[3], ~op[2], ~op[1], ~op[0]);  // AND_Gate
  and and_59 (and_59_out, op[5], ~op[4], ~op[3], ~op[2], op[1], op[0]);  // AND_Gate
  and and_60 (and_60_out, ~Funct[5], ~Funct[4], Funct[3], ~Funct[2], ~Funct[1], ~Funct[0]);  // AND_Gate
  and and_61 (and_61_out, ~Funct[5], ~Funct[4], Funct[3], Funct[2], ~Funct[1], ~Funct[0]);  // AND_Gate
  and and_62 (and_62_out, ~Funct[5], ~Funct[4], ~Funct[3], ~Funct[2], Funct[1], ~Funct[0]);  // AND_Gate
  and and_63 (and_63_out, ~Funct[5], ~Funct[4], ~Funct[3], ~Funct[2], ~Funct[1], ~Funct[0]);  // AND_Gate
  or or_6 (or_10_out[3], and_33_out, and_34_out);
  or or_7 (or_10_out[2], and_35_out, and_36_out, and_37_out, and_38_out, and_39_out, and_40_out, and_41_out, and_42_out, and_43_out, and_44_out, and_45_out);
  Multiplexer #(.select(1), .width(1), .disabled("Z"), .enable("false")) multiplexer_1 (
    .in0(1'b0), .in1(and_60_out), .out(IsJR), .sel(IsSpecial));
  Multiplexer #(.select(1), .width(1), .disabled("Z"), .enable("false")) multiplexer_2 (
    .in0(1'b0), .in1(and_61_out), .out(IsSyscal), .sel(IsSpecial));
  and and_64 (and_64_out, ~Funct[5], ~Funct[4], ~Funct[3], ~Funct[2], Funct[1], Funct[0]);  // AND_Gate
  or or_8 (or_10_out[1], and_46_out, and_47_out);
  or or_9 (or_9_out, and_64_out, and_62_out, and_63_out);
  or or_10 (or_10_out[0], and_48_out, and_49_out, and_50_out, and_51_out, and_52_out, and_53_out, and_54_out, and_55_out, and_56_out, and_57_out, and_58_out, and_59_out);
  Multiplexer #(.select(1), .width(1), .disabled("Z"), .enable("false")) multiplexer_3 (
    .in0(1'b0), .in1(or_9_out), .out(IsShamt), .sel(IsSpecial));
  and and_65 (and_65_out, Funct[5], ~Funct[4], ~Funct[3], Funct[2], ~Funct[1], Funct[0]);  // AND_Gate
  and and_66 (and_66_out, Funct[5], ~Funct[4], ~Funct[3], Funct[2], Funct[1], Funct[0]);  // AND_Gate
  and and_67 (and_67_out, Funct[5], ~Funct[4], Funct[3], ~Funct[2], Funct[1], ~Funct[0]);  // AND_Gate
  and and_68 (and_68_out, Funct[5], ~Funct[4], Funct[3], ~Funct[2], Funct[1], Funct[0]);  // AND_Gate
  and and_69 (and_69_out, Funct[5], ~Funct[4], ~Funct[3], ~Funct[2], ~Funct[1]);  // AND_Gate
  and and_70 (and_70_out, Funct[5], ~Funct[4], ~Funct[3], ~Funct[2], ~Funct[0]);  // AND_Gate
  and and_71 (and_71_out, Funct[5], ~Funct[4], ~Funct[3], ~Funct[1], ~Funct[0]);  // AND_Gate
  and and_72 (and_72_out, Funct[5], ~Funct[4], Funct[3], ~Funct[2], Funct[1], Funct[0]);  // AND_Gate
  and and_73 (and_73_out, Funct[5], ~Funct[4], ~Funct[3], ~Funct[2], Funct[1], ~Funct[0]);  // AND_Gate
  and and_74 (and_74_out, Funct[5], ~Funct[4], ~Funct[3], Funct[2], ~Funct[1], ~Funct[0]);  // AND_Gate
  and and_75 (and_75_out, ~Funct[5], ~Funct[4], ~Funct[3], ~Funct[2], Funct[1], ~Funct[0]);  // AND_Gate
  and and_76 (and_76_out, Funct[5], ~Funct[4], ~Funct[3], Funct[2], Funct[1], Funct[0]);  // AND_Gate
  and and_77 (and_77_out, Funct[5], ~Funct[4], Funct[3], ~Funct[2], Funct[1], ~Funct[0]);  // AND_Gate
  and and_78 (and_78_out, ~Funct[5], ~Funct[4], ~Funct[3], ~Funct[2], Funct[1], Funct[0]);  // AND_Gate
  and and_79 (and_79_out, Funct[5], ~Funct[4], ~Funct[3], ~Funct[2], ~Funct[1]);  // AND_Gate
  and and_80 (and_80_out, Funct[5], ~Funct[4], ~Funct[3], ~Funct[1], ~Funct[0]);  // AND_Gate
  and and_81 (and_81_out, Funct[5], ~Funct[4], Funct[3], ~Funct[2], Funct[1], ~Funct[0]);  // AND_Gate
  or or_11 (or_14_out[3], and_65_out, and_66_out, and_67_out, and_68_out);
  or or_12 (or_14_out[2], and_69_out, and_70_out, and_71_out, and_72_out);
  or or_13 (or_14_out[1], and_73_out, and_74_out, and_75_out, and_76_out, and_77_out);
  or or_14 (or_14_out[0], and_78_out, and_79_out, and_80_out, and_81_out);
  Multiplexer #(.select(1), .width(4), .disabled("Z"), .enable("false")) multiplexer_4 (
    .in0(or_14_out), .in1(or_10_out), .out(out_18), .sel(not_1_out));
  not not_1 (not_1_out, IsSpecial);

  // Other names for the same wires on the sheet: ALUop[3:0] = out_18; Funct5 = Funct[0]; Funct4 = Funct[1];
  //   Funct3 = Funct[2]; Funct2 = Funct[3]; Funct1 = Funct[4]; Funct0 = Funct[5]; op5 = op[0]; op4 = op[1];
  //   op3 = op[2]; op2 = op[3]; op1 = op[4]; op0 = op[5]
endmodule

module Cop0 (
  input  ExpSrc0,
  input  ExpSrc1,
  input  ExpSrc2,
  input  clk,
  input  enable,
  input  [31:0] Inst,
  input  [31:0] PCin,
  input  [31:0] Din,
  output ExRegWrite,
  output ExpBlock,
  output IsEret,
  output HasExp,
  output [31:0] PCout,
  output [31:0] Dout
);

  wire and_2_out, and_4_out, and_5_out, and_6_out, BlockSrc0, BlockSrc1, BlockSrc2, counter_1_q, counter_2_q,
       demultiplexer_1_out0, demultiplexer_1_out1, demultiplexer_1_out2, ExpClick, multiplexer_1_out,
       multiplexer_3_out, multiplexer_4_out, not_2_out, not_3_out, or_1_out, or_2_out;
  wire [31:0] controlled_buffer_1_out, multiplexer_2_out, register_3_q;
  wire [31:1] register_1_q;
  wire [31:3] register_2_q;

  not not_1 (ExRegWrite, Inst[23]);
  and and_1 (IsEret, ~Inst[0], Inst[1], Inst[2], ~Inst[3], ~Inst[4], ~Inst[5]);  // AND_Gate
  not not_2 (not_2_out, HasExp);
  and and_2 (and_2_out, enable, ~ExRegWrite);  // AND_Gate
  Multiplexer #(.select(1), .width(1), .disabled("Z"), .enable("false")) multiplexer_1 (
    .in0(ExpSrc0), .in1(1'b0), .out(multiplexer_1_out), .sel(BlockSrc0));
  Multiplexer #(.select(1), .width(32), .disabled("Z"), .enable("false")) multiplexer_2 (
    .in0(PCin), .in1(Din), .out(multiplexer_2_out), .sel(not_2_out));
  assign controlled_buffer_1_out = ExpSrc0 ? 32'h1 : 32'bz;  // Controlled_Buffer controlled_buffer_1
  assign controlled_buffer_1_out = ExpSrc1 ? 32'h3 : 32'bz;  // Controlled_Buffer controlled_buffer_2
  assign controlled_buffer_1_out = ExpSrc2 ? 32'h7 : 32'bz;  // Controlled_Buffer controlled_buffer_3
  Demultiplexer #(.select(2), .width(1), .tristate("false"), .disabled("Z"), .enable("false")) demultiplexer_1 (
    .out0(demultiplexer_1_out0), .out1(demultiplexer_1_out1), .out2(demultiplexer_1_out2), .in(1'b1),
    .sel(Inst[12:11]));  // open: out3
  or or_1 (or_1_out, multiplexer_1_out, multiplexer_3_out, multiplexer_4_out);
  and and_3 (ExpClick, or_1_out, ~ExpBlock);  // AND_Gate
  Multiplexer #(.select(1), .width(1), .disabled("Z"), .enable("false")) multiplexer_3 (
    .in0(ExpSrc1), .in1(1'b0), .out(multiplexer_3_out), .sel(BlockSrc1));
  and and_4 (and_4_out, and_2_out, demultiplexer_1_out0);
  and and_5 (and_5_out, and_2_out, demultiplexer_1_out1);
  Register #(.width(32), .trigger("rising"), .Select("low")) register_1 (
    .D(Din), .en(and_5_out), .Q({register_1_q, ExpBlock}), .clk(clk));  // open: clr
  Register #(.width(32), .trigger("rising"), .Select("low")) register_2 (
    .D(Din), .en(and_6_out), .Q({register_2_q, BlockSrc2, BlockSrc1, BlockSrc0}), .clk(clk));  // open: clr
  or or_2 (or_2_out, HasExp, and_4_out);
  and and_6 (and_6_out, and_2_out, demultiplexer_1_out2);
  Register #(.width(32), .trigger("rising"), .Select("low")) register_3 (
    .D(controlled_buffer_1_out), .Q(register_3_q), .clk(ExpClick));  // open: en, clr
  Counter #(.width(1), .max('h1), .ongoal("stay"), .trigger("rising"), .behavior("old")) counter_1 (
    .Q(counter_1_q), .clk(ExpClick), .clr(counter_2_q));  // open: load, D, count, carry, preset
  Multiplexer #(.select(1), .width(1), .disabled("Z"), .enable("false")) multiplexer_4 (
    .in0(ExpSrc2), .in1(1'b0), .out(multiplexer_4_out), .sel(BlockSrc2));
  Register #(.width(32), .trigger("low"), .Select("low")) register_4 (
    .D(multiplexer_2_out), .en(or_2_out), .Q(PCout), .clk(clk));  // open: clr
  and and_7 (HasExp, clk, counter_1_q);
  Counter #(.width(1), .max('h1), .ongoal("stay"), .trigger("falling"), .behavior("old")) counter_2 (
    .Q(counter_2_q), .clk(HasExp), .clr(not_3_out));  // open: load, D, count, carry, preset
  not not_3 (not_3_out, counter_1_q);
  Multiplexer #(.select(2), .width(32), .disabled("Z"), .enable("false")) multiplexer_5 (
    .in0(PCout), .in1({register_1_q, ExpBlock}), .in2({register_2_q, BlockSrc2, BlockSrc1, BlockSrc0}),
    .in3(register_3_q), .out(Dout), .sel(Inst[12:11]));

  // Other names for the same wires on the sheet: Sel[1:0] = Inst[12:11]
endmodule

module ImmeExtend (
  input  [15:0] in_1,
  input  zeroExtend,
  output [31:0] out_3
);

  wire [31:0] bit_extender_1_out, bit_extender_2_out;

  assign bit_extender_1_out = {{16{in_1[15]}}, in_1};  // Bit_Extender bit_extender_1
  assign bit_extender_2_out = {{16{1'b0}}, in_1};  // Bit_Extender bit_extender_2
  Multiplexer #(.select(1), .width(32), .disabled("Z"), .enable("false")) multiplexer_1 (
    .in0(bit_extender_1_out), .in1(bit_extender_2_out), .out(out_3), .sel(zeroExtend));
endmodule
